# Fritzing sketch iot_fritzing_chapter_03_06 (saved by Fritzing 0.9.2b)
breadboards: 1

parts:
  Intel_Galileo_Gen_2 = Intel Galileo Gen2
  LED1 = LED - 5mm [color="Green (555nm)" package="5 mm [THT]"]
  R1 = Resistor [tolerance=±5% resistance=270 package=THT]
  LED2 = LED - 5mm [color="Green (555nm)" package="5 mm [THT]"]
  R2 = Resistor [tolerance=±5% resistance=270 package=THT]
  LED3 = LED - 5mm [color="Green (555nm)" package="5 mm [THT]"]
  R3 = Resistor [tolerance=±5% resistance=270 package=THT]
  LED4 = LED - 5mm [color="White (6500K)" package="5 mm [THT]"]
  LED5 = LED - 5mm [color="White (6500K)" package="5 mm [THT]"]
  LED6 = LED - 5mm [color="White (6500K)" package="5 mm [THT]"]
  R7 = Resistor [tolerance=±5% resistance=270 package=THT]
  LED7 = LED - 5mm [color="Red (635nm)" package="5 mm [THT]"]
  LED8 = LED - 5mm [color="Red (635nm)" package="5 mm [THT]"]
  LED9 = LED - 5mm [color="Red (635nm)" package="5 mm [THT]"]
  R8 = Resistor [tolerance=±5% resistance=270 package=THT]
  R9 = Resistor [tolerance=±5% resistance=270 package=THT]
  R4 = Resistor [tolerance=±5% resistance=270 package=THT]
  R5 = Resistor [tolerance=±5% resistance=270 package=THT]
  R6 = Resistor [tolerance=±5% resistance=270 package=THT]

nets:
  N1: Intel_Galileo_Gen_2.D8, R2.Pin_1
  N2: Intel_Galileo_Gen_2.D9_PWM, R1.Pin_1
  N3: Intel_Galileo_Gen_2.GND, LED1.cathode, LED2.cathode, LED3.cathode, LED4.cathode, LED5.cathode, LED6.cathode, LED7.cathode, LED8.cathode, LED9.cathode
  N4: Intel_Galileo_Gen_2.D1/TX, R9.Pin_1
  N5: Intel_Galileo_Gen_2.D2, R8.Pin_1
  N6: Intel_Galileo_Gen_2.D3_PWM, R7.Pin_1
  N7: Intel_Galileo_Gen_2.D4, R6.Pin_1
  N8: Intel_Galileo_Gen_2.D5_PWM, R5.Pin_1
  N9: Intel_Galileo_Gen_2.D6_PWM, R4.Pin_1
  N10: Intel_Galileo_Gen_2.D7, R3.Pin_1
  N11: LED1.anode, R1.Pin_0
  N12: LED2.anode, R2.Pin_0
  N13: LED3.anode, R3.Pin_0
  N14: LED4.anode, R4.Pin_0
  N15: LED5.anode, R5.Pin_0
  N16: LED6.anode, R6.Pin_0
  N17: R7.Pin_0, LED7.anode
  N18: LED8.anode, R8.Pin_0
  N19: LED9.anode, R9.Pin_0
