# Fritzing sketch iot_fritzing_chapter_04_02 (saved by Fritzing 0.9.2b)
breadboards: 1

parts:
  Intel_Galileo_Gen_2 = Intel Galileo Gen2
  LED1 = LED - 5mm [color="Red (633nm)" package="5 mm [THT]"]
  LED2 = LED - 5mm [color="Green (555nm)" package="5 mm [THT]"]
  R2 = Resistor [tolerance=±5% resistance=270 package=THT]
  LED3 = LED - 5mm [color="Blue (470nm)" package="5 mm [THT]"]
  R3 = Resistor [tolerance=±5% resistance=270 package=THT]
  R1 = Resistor [tolerance=±5% resistance=270 package=THT]

nets:
  N1: Intel_Galileo_Gen_2.GND, LED1.cathode, LED2.cathode, LED3.cathode
  N2: Intel_Galileo_Gen_2.D3_PWM, R3.Pin_1
  N3: Intel_Galileo_Gen_2.D5_PWM, R2.Pin_1
  N4: Intel_Galileo_Gen_2.D6_PWM, R1.Pin_1
  N5: LED1.anode, R1.Pin_0
  N6: LED2.anode, R2.Pin_0
  N7: LED3.anode, R3.Pin_0

notes:
  Pin ~6 to connect the red LED
  Pin ~5 to connect the green LED
  Pin ~3 to connect the blue LED.
