# Fritzing sketch iot_fritzing_chapter_04_03 (saved by Fritzing 0.9.2b)
breadboards: 1

parts:
  Intel_Galileo_Gen_2 = Intel Galileo Gen2
  R2 = Resistor [tolerance=±5% resistance=270 package=THT]
  R3 = Resistor [tolerance=±5% resistance=270 package=THT]
  R1 = Resistor [tolerance=±5% resistance=270 package=THT]
  RGBLED1 = RGB LED (com. cathode, rgb) [package="5 mm [THT]"]

nets:
  N1: Intel_Galileo_Gen_2.GND, RGBLED1.common_cathode
  N2: Intel_Galileo_Gen_2.D3_PWM, R3.Pin_1
  N3: Intel_Galileo_Gen_2.D5_PWM, R2.Pin_1
  N4: Intel_Galileo_Gen_2.D6_PWM, R1.Pin_1
  N5: R2.Pin_0, RGBLED1.green_anode
  N6: R3.Pin_0, RGBLED1.blue_anode
  N7: R1.Pin_0, RGBLED1.red_anode

notes:
  Pin ~6 to connect the red LED
  Pin ~5 to connect the green LED
  Pin ~3 to connect the blue LED.
