# Fritzing sketch iot_fritzing_chapter_05_01 (saved by Fritzing 0.9.2b)
breadboards: 1

parts:
  Intel_Galileo_Gen_2 = Intel Galileo Gen2
  S1 = Pushbutton [package=THT]
  R1 = Resistor [tolerance=±5% resistance=120 package=THT]

nets:
  N1: Intel_Galileo_Gen_2.GND, S1.leg0
  N2: Intel_Galileo_Gen_2.D0/RX, S1.leg1, R1.Pin_0
  N3: Intel_Galileo_Gen_2.ioref, R1.Pin_1
