# Fritzing sketch iot_fritzing_chapter_05_03 (saved by Fritzing 0.9.2b)
breadboards: 1

parts:
  Intel_Galileo_Gen_2 = Intel Galileo Gen2
  R2 = Resistor [tolerance=±5% resistance=270 package=THT]
  R3 = Resistor [tolerance=±5% resistance=270 package=THT]
  R1 = Resistor [tolerance=±5% resistance=270 package=THT]
  RGBLED1 = RGB LED (com. cathode, rgb) [package="5 mm [THT]"]
  S1 = Pushbutton [package=THT]
  S2 = Pushbutton [package=THT]
  R4 = Resistor [tolerance=±5% resistance=120 package=THT]
  R5 = Resistor [tolerance=±5% resistance=120 package=THT]

nets:
  N1: Intel_Galileo_Gen_2.GND, RGBLED1.common_cathode, S1.leg0, S2.leg0
  N2: Intel_Galileo_Gen_2.D0/RX, S2.leg1, R5.Pin_0
  N3: Intel_Galileo_Gen_2.D1/TX, S1.leg1, R4.Pin_0
  N4: Intel_Galileo_Gen_2.D3_PWM, R3.Pin_1
  N5: Intel_Galileo_Gen_2.D5_PWM, R2.Pin_1
  N6: Intel_Galileo_Gen_2.D6_PWM, R1.Pin_1
  N7: Intel_Galileo_Gen_2.ioref, R4.Pin_1, R5.Pin_1
  N8: R2.Pin_0, RGBLED1.green_anode
  N9: R3.Pin_0, RGBLED1.blue_anode
  N10: R1.Pin_0, RGBLED1.red_anode

notes:
  Pin ~6 to connect the red LED
  Pin ~5 to connect the green LED
  Pin ~3 to connect the blue LED.
