# Fritzing sketch iot_fritzing_chapter_06_01 (saved by Fritzing 0.9.2b)
breadboards: 1

parts:
  Board = Intel Galileo Gen2
  VCC1 = Battery
  R1 = Resistor [tolerance=±5% resistance=2.2k package=THT]

nets:
  N1: Board.A0, R1.Pin_0
  N2: Board.GND, VCC1.-
  N3: VCC1.+, R1.Pin_1
