# Fritzing sketch iot_fritzing_chapter_06_02 (saved by Fritzing 0.9.2b)
breadboards: 1

parts:
  Board = Intel Galileo Gen2
  R1 = Resistor [tolerance=±5% resistance=10k package=THT]
  LDR1 = Photocell (LDR) [package=THT]

nets:
  N1: Board.A0, R1.Pin_1, LDR1.pin_0
  N2: Board.GND, R1.Pin_0
  N3: Board.ioref, LDR1.pin_1
