# Fritzing sketch iot_fritzing_chapter_06_03 (saved by Fritzing 0.9.2b)
breadboards: 1

parts:
  Board = Intel Galileo Gen2
  R1 = Resistor [tolerance=±5% resistance=10k package=THT]
  LDR1 = Photocell (LDR) [package=THT]
  RGBLED1 = RGB LED (com. cathode, rgb) [package="5 mm [THT]"]
  R2 = Resistor [tolerance=±5% resistance=270 package=THT]
  R3 = Resistor [tolerance=±5% resistance=270 package=THT]
  R4 = Resistor [tolerance=±5% resistance=270 package=THT]

nets:
  N1: Board.A0, R1.Pin_1, LDR1.pin_0
  N2: Board.GND, R1.Pin_0, RGBLED1.common_cathode
  N3: Board.D3_PWM, R4.Pin_1
  N4: Board.D5_PWM, R3.Pin_1
  N5: Board.D6_PWM, R2.Pin_1
  N6: Board.ioref, LDR1.pin_1
  N7: RGBLED1.red_anode, R2.Pin_0
  N8: RGBLED1.green_anode, R3.Pin_0
  N9: RGBLED1.blue_anode, R4.Pin_0
