# Fritzing sketch iot_fritzing_chapter_07_01 (saved by Fritzing 0.9.2b)
breadboards: 1

parts:
  Board = Intel Galileo Gen2
  Part1 = Triple Axis Accelerometer Breakout - ADXL335

nets:
  N1: Board.A0, Part1.XOUT
  N2: Board.A1, Part1.YOUT
  N3: Board.A2, Part1.ZOUT
  3V3: Board.3V3, Part1.VCC
  GND: Board.GND, Part1.GND
