# Fritzing sketch iot_fritzing_chapter_07_02 (saved by Fritzing 0.9.2b)
breadboards: 1

parts:
  Board = Intel Galileo Gen2
  I2C_Accelerometer = Grove 3 Axis Digital Accelerometer 16g

nets:
  GND: Board.GND, I2C_Accelerometer.GND
  N1: Board.A4/SDA, I2C_Accelerometer.SDA
  N2: Board.A5/SCL, I2C_Accelerometer.SCL
  5V: Board.5V, I2C_Accelerometer.VCC
