# Fritzing sketch iot_fritzing_chapter_07_03 (saved by Fritzing 0.9.2b)
breadboards: 1

parts:
  Board = Intel Galileo Gen2
  Analog_temperature_sensor = Grove Temperature Sensor

nets:
  N1: Board.A0, Analog_temperature_sensor.SIG
  GND: Board.GND, Analog_temperature_sensor.GND
  3V3: Board.3V3, Analog_temperature_sensor.VCC
