# Fritzing sketch iot_fritzing_chapter_07_05 (saved by Fritzing 0.9.2b)
breadboards: 1

parts:
  Board = Intel Galileo Gen2
  I2C_Temperature_and_humidity_sensor = Grove 3 Axis Digital Accelerometer 16g

nets:
  GND: Board.GND, I2C_Temperature_and_humidity_sensor.GND
  N1: Board.A4/SDA, I2C_Temperature_and_humidity_sensor.SDA
  N2: Board.A5/SCL, I2C_Temperature_and_humidity_sensor.SCL
  3V3: Board.3V3, I2C_Temperature_and_humidity_sensor.VCC
