# Fritzing sketch iot_fritzing_chapter_08_03 (saved by Fritzing 0.9.2b)
breadboards: 1

parts:
  Board = Intel Galileo Gen2
  I2C_Temperature_and_humidity_sensor = Grove 3 Axis Digital Accelerometer 16g
  I2C_16x2_LCD_backlight = Grove OLED 128x96
  Standard_servo = Basic Servo

nets:
  N1: Board.A5/SCL, I2C_Temperature_and_humidity_sensor.SCL, I2C_16x2_LCD_backlight.SCL
  GND: Board.GND, I2C_Temperature_and_humidity_sensor.GND, I2C_16x2_LCD_backlight.GND, Standard_servo.gnd
  N2: Board.A4/SDA, I2C_Temperature_and_humidity_sensor.SDA, I2C_16x2_LCD_backlight.SDA
  N3: Board.D3_PWM, Standard_servo.pulse
  3V3: Board.3V3, I2C_Temperature_and_humidity_sensor.VCC
  VCC: Board.5V, I2C_16x2_LCD_backlight.VCC, Standard_servo.vcc
